# Fritzing sketch Momentary (saved by Fritzing 0.9.3b)
breadboards: 1

parts:
  Mod1 = Raspberry Pi Pico
  S4 = Round Pushbutton
  LED1 = smd LED [color="Red (633nm)" package="0603 [SMD]"]
  R1 = Resistor [tolerance=±5% resistance=220 package="2010 [SMD]"]

nets:
  N1: Mod1.pin_3, Mod1.pin_8, Mod1.pin_13, Mod1.pin_18, Mod1.pin_23, Mod1.pin_28, Mod1.pin_33, Mod1.pin_38, Mod1.pin_42, R1.Pin_1
  N2: Mod1.pin_17, LED1.anode
  N3: Mod1.pin_20, S4.leg0
  N4: Mod1.pin_36, S4.leg1
  N5: LED1.cathode, R1.Pin_0

custom parts:
  Raspberry Pi Pico: Raspberry Pi Pico. Based around the RP2040 microcontroller the Pico is a low cost microcontroller device bringing Raspberry Pi quality, cost, and easy of use to the microcontroller space. Jan 2021, Split part in to two versions: tht (this one) and SMD. This one will drill holes for a .1 in header in pcb to allow plugging in the module as well as providing pads to solder the module to the top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

// code stored in the sketch: Pushbutton Coe.py.ino
# Momentary Switch - Polling with comparision to previous state of switch to prevent bounce and repeats
# Good example to mimic the function of a TOGGLE SWITCH or a ROCKER SWITCH

#Connect wire #1 to Pin 36/3.3V
#Connect wire #2 to Pin 20/GP15

#load libraries
import machine
import utime

#This is needed to indicate the state of the toggle switch
Toggle_Indicator_LED = machine.Pin(25,machine.Pin.OUT) #use on board LED to show switch state

# Using a try: statement to apply the internal LED depending on Pico Type/Python Code version
try:
    pico_led = LED("LED", pwm=False)
except TypeError:
    # older version of micropython before "LED" was supported
    pico_led = LED(25, pwm=False)

#Create a variable to hold the state of the "Toggle Switch"
Toggle_State = False
Toggle_Indicator_LED.value(False)

#Create an 'object' for our actual Momentary Button
Toggle_Sw = machine.Pin(15,machine.Pin.IN,machine.Pin.PULL_DOWN)
#Create a variable to hold Last State
Toggle_Sw_Prev_State = Toggle_Sw.value()

def Toggle_Btn_Handler():
    global Toggle_Sw_Prev_State
    global Toggle_State
    #utime.sleep_ms(1)  #If the switch has a lot of bounce- a dwell here can help
    if (Toggle_Sw.value() == True) and (Toggle_Sw_Prev_State == False): #Pressed, If input is HIGH and different from before
        Toggle_Sw_Prev_State = True              #Update previous state variable
        if Toggle_State == False: #Was OFF, now turn it ON
            Toggle_State = True
        elif Toggle_State == True: # Was ON, now turn it OFF
            Toggle_State = False
        Toggle_Indicator_LED.value(Toggle_State)
    elif (Toggle_Sw.value() == False) and (Toggle_Sw_Prev_State == True): #Released, If input is LOW and different from before
        Toggle_Sw_Prev_State = False             #Update previous state variable


print("Ready, Set, Go!")
while True:  #run an endless loop - Typical main loop
    Toggle_Btn_Handler()   
    #utime.sleep(.01) #slow down the loop to mimic other processing activities
